// Logisim project BasketBall Scoreboard.circ as structural Verilog
module main (
  input  clear,
  input  Start,
  input  in_3,
  input  in_4,
  output out_5
);

  wire and_1_out, and_2_out, and_3_out, and_4_out, and_5_out, and_6_out, and_7_out, and_8_out, and_9_out,
       button_1_out, button_2_out, clock_1_out, clock_2_out, comparator_1_out_26, comparator_1_out_27,
       counter_1_out_3, counter_1_out_4, counter_1_out_5, counter_1_out_6, counter_1_out_7, decade1_1_out_4,
       decade1_1_out_5, decade1_1_out_6, decade1_1_out_7, decade1_1_out_8, decade1_1_out_9, decade1_1_out_10,
       decade1_1_out_11, decade1_1_out_12, decade1_1_out_13, decade1_1_out_14, decade1_1_out_15,
       decade1_2_out_4, decade1_2_out_5, decade1_2_out_6, decade1_2_out_7, decade1_2_out_8, decade1_2_out_9,
       decade1_2_out_10, decade1_2_out_11, decade1_2_out_12, decade1_2_out_13, decade1_2_out_14,
       decade1_2_out_15, decade_1_out_4, decade_1_out_5, decade_1_out_6, decade_1_out_7, decade_1_out_8,
       decade_1_out_9, decade_1_out_10, decade_1_out_11, decade_2_out_4, decade_2_out_5, decade_2_out_6,
       decade_2_out_7, decade_2_out_8, decade_2_out_9, decade_2_out_10, decade_2_out_11, decade_3_out_4,
       decade_3_out_5, decade_3_out_6, decade_3_out_7, decade_3_out_8, decade_3_out_9, decade_3_out_10,
       decade_3_out_11, decade_4_out_4, decade_4_out_5, decade_4_out_6, decade_4_out_7, decade_4_out_8,
       decade_4_out_9, decade_4_out_10, decade_4_out_11, decade_5_out_4, decade_5_out_5, decade_5_out_6,
       decade_5_out_7, decade_5_out_8, decade_5_out_9, decade_5_out_10, decade_5_out_11, decade_6_out_4,
       decade_6_out_5, decade_6_out_6, decade_6_out_7, decade_6_out_8, decade_6_out_9, decade_6_out_10,
       decade_6_out_11, decade_7_out_4, decade_7_out_5, decade_7_out_6, decade_7_out_7, decade_7_out_8,
       decade_7_out_9, decade_7_out_10, decade_7_out_11, decade_8_out_4, decade_8_out_5, decade_8_out_6,
       decade_8_out_7, decade_8_out_8, decade_8_out_9, decade_8_out_10, decade_8_out_11, n7_segemnt_1_a,
       n7_segemnt_1_b, n7_segemnt_1_c, n7_segemnt_1_d, n7_segemnt_1_e, n7_segemnt_1_f, n7_segemnt_1_g,
       n7_segemnt_2_a, n7_segemnt_2_b, n7_segemnt_2_c, n7_segemnt_2_d, n7_segemnt_2_e, n7_segemnt_2_f,
       n7_segemnt_2_g, n7_segemnt_3_a, n7_segemnt_3_b, n7_segemnt_3_c, n7_segemnt_3_d, n7_segemnt_3_e,
       n7_segemnt_3_f, n7_segemnt_3_g, n7_segemnt_4_a, n7_segemnt_4_b, n7_segemnt_4_c, n7_segemnt_4_d,
       n7_segemnt_4_e, n7_segemnt_4_f, n7_segemnt_4_g, n7_segemnt_5_a, n7_segemnt_5_b, n7_segemnt_5_c,
       n7_segemnt_5_d, n7_segemnt_5_e, n7_segemnt_5_f, n7_segemnt_5_g, n7_segemnt_6_a, n7_segemnt_6_b,
       n7_segemnt_6_c, n7_segemnt_6_d, n7_segemnt_6_e, n7_segemnt_6_f, n7_segemnt_6_g, n7_segemnt_7_a,
       n7_segemnt_7_b, n7_segemnt_7_c, n7_segemnt_7_d, n7_segemnt_7_e, n7_segemnt_7_f, n7_segemnt_7_g,
       n7_segemnt_8_a, n7_segemnt_8_b, n7_segemnt_8_c, n7_segemnt_8_d, n7_segemnt_8_e, n7_segemnt_8_f,
       n7_segemnt_8_g, n7_segemnt_9_a, n7_segemnt_9_b, n7_segemnt_9_c, n7_segemnt_9_d, n7_segemnt_9_e,
       n7_segemnt_9_f, n7_segemnt_9_g, n7_segemnt_10_a, n7_segemnt_10_b, n7_segemnt_10_c, n7_segemnt_10_d,
       n7_segemnt_10_e, n7_segemnt_10_f, n7_segemnt_10_g, n7_segemnt_11_a, n7_segemnt_11_b, n7_segemnt_11_c,
       n7_segemnt_11_d, n7_segemnt_11_e, n7_segemnt_11_f, n7_segemnt_11_g, n7_segemnt_12_a, n7_segemnt_12_b,
       n7_segemnt_12_c, n7_segemnt_12_d, n7_segemnt_12_e, n7_segemnt_12_f, n7_segemnt_12_g, n7_segemnt_13_a,
       n7_segemnt_13_b, n7_segemnt_13_c, n7_segemnt_13_d, n7_segemnt_13_e, n7_segemnt_13_f, n7_segemnt_13_g,
       n7_segemnt_14_a, n7_segemnt_14_b, n7_segemnt_14_c, n7_segemnt_14_d, n7_segemnt_14_e, n7_segemnt_14_f,
       n7_segemnt_14_g, n7_segemnt_15_a, n7_segemnt_15_b, n7_segemnt_15_c, n7_segemnt_15_d, n7_segemnt_15_e,
       n7_segemnt_15_f, n7_segemnt_15_g, n7_segemnt_16_a, n7_segemnt_16_b, n7_segemnt_16_c, n7_segemnt_16_d,
       n7_segemnt_16_e, n7_segemnt_16_f, n7_segemnt_16_g, n7_segemnt_17_a, n7_segemnt_17_b, n7_segemnt_17_c,
       n7_segemnt_17_d, n7_segemnt_17_e, n7_segemnt_17_f, n7_segemnt_17_g, n7_segemnt_18_a, n7_segemnt_18_b,
       n7_segemnt_18_c, n7_segemnt_18_d, n7_segemnt_18_e, n7_segemnt_18_f, n7_segemnt_18_g, n7_segemnt_19_a,
       n7_segemnt_19_b, n7_segemnt_19_c, n7_segemnt_19_d, n7_segemnt_19_e, n7_segemnt_19_f, n7_segemnt_19_g,
       n7_segemnt_20_a, n7_segemnt_20_b, n7_segemnt_20_c, n7_segemnt_20_d, n7_segemnt_20_e, n7_segemnt_20_f,
       n7_segemnt_20_g, n7_segemnt_21_a, n7_segemnt_21_b, n7_segemnt_21_c, n7_segemnt_21_d, n7_segemnt_21_e,
       n7_segemnt_21_f, n7_segemnt_21_g, n7_segemnt_22_a, n7_segemnt_22_b, n7_segemnt_22_c, n7_segemnt_22_d,
       n7_segemnt_22_e, n7_segemnt_22_f, n7_segemnt_22_g, or_1_out;

  or or_1 (or_1_out, counter_1_out_6, counter_1_out_5, counter_1_out_4, counter_1_out_3);
  Clock clock_1 (.out(clock_1_out));
  and and_1 (and_1_out, counter_1_out_4, button_1_out);
  and and_2 (and_2_out, counter_1_out_5, button_1_out);
  and and_3 (and_3_out, counter_1_out_6, button_1_out);
  counter counter_1 (
    .in_1(Start), .in_2(clock_1_out), .out_3(counter_1_out_3), .out_4(counter_1_out_4),
    .out_5(counter_1_out_5), .out_6(counter_1_out_6), .out_7(counter_1_out_7));
  and and_4 (and_4_out, button_1_out, counter_1_out_3);
  _7_Segment_Display u_7_segment_display_1 (
    .g(n7_segemnt_1_g), .f(n7_segemnt_1_f), .a(n7_segemnt_1_a), .b(n7_segemnt_1_b), .e(n7_segemnt_1_e),
    .d(n7_segemnt_1_d), .c(n7_segemnt_1_c));  // open: dp
  _7_segemnt u_7_segemnt_1 (
    .f(n7_segemnt_1_f), .g(n7_segemnt_1_g), .e(n7_segemnt_1_e), .d(n7_segemnt_1_d), .c(n7_segemnt_1_c),
    .b(n7_segemnt_1_b), .a(n7_segemnt_1_a), .in_1(decade1_1_out_15), .in_2(decade1_1_out_14),
    .in_3(decade1_1_out_13), .in_4(decade1_1_out_12));
  decade1 decade1_1 (
    .in_1(and_5_out), .in_2(button_1_out), .in_3(in_4), .out_4(decade1_1_out_4), .out_5(decade1_1_out_5),
    .out_6(decade1_1_out_6), .out_7(decade1_1_out_7), .out_8(decade1_1_out_8), .out_9(decade1_1_out_9),
    .out_10(decade1_1_out_10), .out_11(decade1_1_out_11), .out_12(decade1_1_out_12),
    .out_13(decade1_1_out_13), .out_14(decade1_1_out_14), .out_15(decade1_1_out_15));
  _7_Segment_Display u_7_segment_display_2 (
    .g(n7_segemnt_2_g), .f(n7_segemnt_2_f), .a(n7_segemnt_2_a), .b(n7_segemnt_2_b), .e(n7_segemnt_2_e),
    .d(n7_segemnt_2_d), .c(n7_segemnt_2_c));  // open: dp
  _7_segemnt u_7_segemnt_2 (
    .f(n7_segemnt_2_f), .g(n7_segemnt_2_g), .e(n7_segemnt_2_e), .d(n7_segemnt_2_d), .c(n7_segemnt_2_c),
    .b(n7_segemnt_2_b), .a(n7_segemnt_2_a), .in_1(decade1_1_out_11), .in_2(decade1_1_out_10),
    .in_3(decade1_1_out_9), .in_4(decade1_1_out_8));
  _7_Segment_Display u_7_segment_display_3 (
    .g(comparator_1_out_27), .f(comparator_1_out_27), .a(comparator_1_out_27), .b(comparator_1_out_27),
    .e(comparator_1_out_27), .c(comparator_1_out_27));  // open: d, dp
  Clock clock_2 (.out(clock_2_out));
  Button button_1 (.out(button_1_out));
  and and_5 (and_5_out, Start, counter_1_out_7);
  decade decade_1 (
    .in_1(and_5_out), .in_2(and_4_out), .in_3(clear), .out_4(decade_1_out_4), .out_5(decade_1_out_5),
    .out_6(decade_1_out_6), .out_7(decade_1_out_7), .out_8(decade_1_out_8), .out_9(decade_1_out_9),
    .out_10(decade_1_out_10), .out_11(decade_1_out_11));
  and and_6 (and_6_out, counter_1_out_3, button_2_out);
  decade decade_2 (
    .in_1(and_5_out), .in_2(and_1_out), .in_3(clear), .out_4(decade_2_out_4), .out_5(decade_2_out_5),
    .out_6(decade_2_out_6), .out_7(decade_2_out_7), .out_8(decade_2_out_8), .out_9(decade_2_out_9),
    .out_10(decade_2_out_10), .out_11(decade_2_out_11));
  decade decade_3 (
    .in_1(and_5_out), .in_2(and_2_out), .in_3(clear), .out_4(decade_3_out_4), .out_5(decade_3_out_5),
    .out_6(decade_3_out_6), .out_7(decade_3_out_7), .out_8(decade_3_out_8), .out_9(decade_3_out_9),
    .out_10(decade_3_out_10), .out_11(decade_3_out_11));
  decade decade_4 (
    .in_1(and_5_out), .in_2(and_3_out), .in_3(clear), .out_4(decade_4_out_4), .out_5(decade_4_out_5),
    .out_6(decade_4_out_6), .out_7(decade_4_out_7), .out_8(decade_4_out_8), .out_9(decade_4_out_9),
    .out_10(decade_4_out_10), .out_11(decade_4_out_11));
  _7_segemnt u_7_segemnt_3 (
    .f(n7_segemnt_3_f), .g(n7_segemnt_3_g), .e(n7_segemnt_3_e), .d(n7_segemnt_3_d), .c(n7_segemnt_3_c),
    .b(n7_segemnt_3_b), .a(n7_segemnt_3_a), .in_1(decade1_1_out_7), .in_2(decade1_1_out_6),
    .in_3(decade1_1_out_5), .in_4(decade1_1_out_4));
  _7_Segment_Display u_7_segment_display_4 (
    .g(n7_segemnt_4_g), .f(n7_segemnt_4_f), .a(n7_segemnt_4_a), .b(n7_segemnt_4_b), .e(n7_segemnt_4_e),
    .d(n7_segemnt_4_d), .c(n7_segemnt_4_c));  // open: dp
  _7_segemnt u_7_segemnt_4 (
    .f(n7_segemnt_4_f), .g(n7_segemnt_4_g), .e(n7_segemnt_4_e), .d(n7_segemnt_4_d), .c(n7_segemnt_4_c),
    .b(n7_segemnt_4_b), .a(n7_segemnt_4_a), .in_1(decade_1_out_11), .in_2(decade_1_out_10),
    .in_3(decade_1_out_9), .in_4(decade_1_out_8));
  _7_Segment_Display u_7_segment_display_5 (
    .g(n7_segemnt_5_g), .f(n7_segemnt_5_f), .a(n7_segemnt_5_a), .b(n7_segemnt_5_b), .e(n7_segemnt_5_e),
    .d(n7_segemnt_5_d), .c(n7_segemnt_5_c));  // open: dp
  _7_segemnt u_7_segemnt_5 (
    .f(n7_segemnt_5_f), .g(n7_segemnt_5_g), .e(n7_segemnt_5_e), .d(n7_segemnt_5_d), .c(n7_segemnt_5_c),
    .b(n7_segemnt_5_b), .a(n7_segemnt_5_a), .in_1(decade_2_out_11), .in_2(decade_2_out_10),
    .in_3(decade_2_out_9), .in_4(decade_2_out_8));
  _7_Segment_Display u_7_segment_display_6 (
    .g(n7_segemnt_6_g), .f(n7_segemnt_6_f), .a(n7_segemnt_6_a), .b(n7_segemnt_6_b), .e(n7_segemnt_6_e),
    .d(n7_segemnt_6_d), .c(n7_segemnt_6_c));  // open: dp
  _7_segemnt u_7_segemnt_6 (
    .f(n7_segemnt_6_f), .g(n7_segemnt_6_g), .e(n7_segemnt_6_e), .d(n7_segemnt_6_d), .c(n7_segemnt_6_c),
    .b(n7_segemnt_6_b), .a(n7_segemnt_6_a), .in_1(decade_3_out_11), .in_2(decade_3_out_10),
    .in_3(decade_3_out_9), .in_4(decade_3_out_8));
  and and_7 (and_7_out, counter_1_out_5, button_2_out);
  _7_Segment_Display u_7_segment_display_7 (
    .g(n7_segemnt_7_g), .f(n7_segemnt_7_f), .a(n7_segemnt_7_a), .b(n7_segemnt_7_b), .e(n7_segemnt_7_e),
    .d(n7_segemnt_7_d), .c(n7_segemnt_7_c));  // open: dp
  _7_segemnt u_7_segemnt_7 (
    .f(n7_segemnt_7_f), .g(n7_segemnt_7_g), .e(n7_segemnt_7_e), .d(n7_segemnt_7_d), .c(n7_segemnt_7_c),
    .b(n7_segemnt_7_b), .a(n7_segemnt_7_a), .in_1(decade_4_out_11), .in_2(decade_4_out_10),
    .in_3(decade_4_out_9), .in_4(decade_4_out_8));
  and and_8 (and_8_out, button_2_out, counter_1_out_6);
  _7_Segment_Display u_7_segment_display_8 (
    .g(n7_segemnt_3_g), .f(n7_segemnt_3_f), .a(n7_segemnt_3_a), .b(n7_segemnt_3_b), .e(n7_segemnt_3_e),
    .d(n7_segemnt_3_d), .c(n7_segemnt_3_c));  // open: dp
  _7_segemnt u_7_segemnt_8 (
    .f(n7_segemnt_8_f), .g(n7_segemnt_8_g), .e(n7_segemnt_8_e), .d(n7_segemnt_8_d), .c(n7_segemnt_8_c),
    .b(n7_segemnt_8_b), .a(n7_segemnt_8_a), .in_1(decade_1_out_7), .in_2(decade_1_out_6),
    .in_3(decade_1_out_5), .in_4(decade_1_out_4));
  _7_segemnt u_7_segemnt_9 (
    .f(n7_segemnt_9_f), .g(n7_segemnt_9_g), .e(n7_segemnt_9_e), .d(n7_segemnt_9_d), .c(n7_segemnt_9_c),
    .b(n7_segemnt_9_b), .a(n7_segemnt_9_a), .in_1(decade_2_out_7), .in_2(decade_2_out_6),
    .in_3(decade_2_out_5), .in_4(decade_2_out_4));
  and and_9 (and_9_out, counter_1_out_4, button_2_out);
  _7_segemnt u_7_segemnt_10 (
    .f(n7_segemnt_10_f), .g(n7_segemnt_10_g), .e(n7_segemnt_10_e), .d(n7_segemnt_10_d), .c(n7_segemnt_10_c),
    .b(n7_segemnt_10_b), .a(n7_segemnt_10_a), .in_1(decade_3_out_7), .in_2(decade_3_out_6),
    .in_3(decade_3_out_5), .in_4(decade_3_out_4));
  _7_Segment_Display u_7_segment_display_9 (
    .g(n7_segemnt_11_g), .f(n7_segemnt_11_f), .a(n7_segemnt_11_a), .b(n7_segemnt_11_b), .e(n7_segemnt_11_e),
    .d(n7_segemnt_11_d), .c(n7_segemnt_11_c));  // open: dp
  _7_segemnt u_7_segemnt_11 (
    .f(n7_segemnt_11_f), .g(n7_segemnt_11_g), .e(n7_segemnt_11_e), .d(n7_segemnt_11_d), .c(n7_segemnt_11_c),
    .b(n7_segemnt_11_b), .a(n7_segemnt_11_a), .in_1(decade_4_out_7), .in_2(decade_4_out_6),
    .in_3(decade_4_out_5), .in_4(decade_4_out_4));
  comparator comparator_1 (
    .in_1(decade1_1_out_12), .in_2(decade1_1_out_13), .in_3(decade1_1_out_14), .in_5(decade1_1_out_15),
    .in_10(decade1_1_out_8), .in_12(decade1_1_out_9), .in_14(decade1_1_out_10), .in_16(decade1_1_out_11),
    .in_19(decade1_1_out_4), .in_21(decade1_1_out_5), .in_23(decade1_1_out_6), .in_24(decade1_1_out_7),
    .out_27(comparator_1_out_27), .out_25(out_5), .out_26(comparator_1_out_26), .in_4(decade1_2_out_12),
    .in_6(decade1_2_out_13), .in_7(decade1_2_out_14), .in_8(decade1_2_out_15), .in_9(decade1_2_out_8),
    .in_11(decade1_2_out_9), .in_13(decade1_2_out_10), .in_15(decade1_2_out_11), .in_17(decade1_2_out_4),
    .in_18(decade1_2_out_5), .in_20(decade1_2_out_6), .in_22(decade1_2_out_7));
  _7_Segment_Display u_7_segment_display_10 (
    .g(n7_segemnt_8_g), .f(n7_segemnt_8_f), .a(n7_segemnt_8_a), .b(n7_segemnt_8_b), .e(n7_segemnt_8_e),
    .d(n7_segemnt_8_d), .c(n7_segemnt_8_c));  // open: dp
  _7_Segment_Display u_7_segment_display_11 (
    .g(n7_segemnt_9_g), .f(n7_segemnt_9_f), .a(n7_segemnt_9_a), .b(n7_segemnt_9_b), .e(n7_segemnt_9_e),
    .d(n7_segemnt_9_d), .c(n7_segemnt_9_c));  // open: dp
  _7_Segment_Display u_7_segment_display_12 (
    .g(n7_segemnt_10_g), .f(n7_segemnt_10_f), .a(n7_segemnt_10_a), .b(n7_segemnt_10_b), .e(n7_segemnt_10_e),
    .d(n7_segemnt_10_d), .c(n7_segemnt_10_c));  // open: dp
  Button button_2 (.out(button_2_out));
  decade decade_5 (
    .in_1(and_5_out), .in_2(and_6_out), .in_3(clear), .out_4(decade_5_out_4), .out_5(decade_5_out_5),
    .out_6(decade_5_out_6), .out_7(decade_5_out_7), .out_8(decade_5_out_8), .out_9(decade_5_out_9),
    .out_10(decade_5_out_10), .out_11(decade_5_out_11));
  decade decade_6 (
    .in_1(and_5_out), .in_2(and_9_out), .in_3(clear), .out_4(decade_6_out_4), .out_5(decade_6_out_5),
    .out_6(decade_6_out_6), .out_7(decade_6_out_7), .out_8(decade_6_out_8), .out_9(decade_6_out_9),
    .out_10(decade_6_out_10), .out_11(decade_6_out_11));
  decade decade_7 (
    .in_1(and_5_out), .in_2(and_7_out), .in_3(clear), .out_4(decade_7_out_4), .out_5(decade_7_out_5),
    .out_6(decade_7_out_6), .out_7(decade_7_out_7), .out_8(decade_7_out_8), .out_9(decade_7_out_9),
    .out_10(decade_7_out_10), .out_11(decade_7_out_11));
  decade decade_8 (
    .in_1(and_5_out), .in_2(and_8_out), .in_3(clear), .out_4(decade_8_out_4), .out_5(decade_8_out_5),
    .out_6(decade_8_out_6), .out_7(decade_8_out_7), .out_8(decade_8_out_8), .out_9(decade_8_out_9),
    .out_10(decade_8_out_10), .out_11(decade_8_out_11));
  _7_Segment_Display u_7_segment_display_13 (
    .g(n7_segemnt_12_g), .f(n7_segemnt_12_f), .a(n7_segemnt_12_a), .b(n7_segemnt_12_b), .e(n7_segemnt_12_e),
    .d(n7_segemnt_12_d), .c(n7_segemnt_12_c));  // open: dp
  _7_segemnt u_7_segemnt_12 (
    .f(n7_segemnt_12_f), .g(n7_segemnt_12_g), .e(n7_segemnt_12_e), .d(n7_segemnt_12_d), .c(n7_segemnt_12_c),
    .b(n7_segemnt_12_b), .a(n7_segemnt_12_a), .in_1(decade1_2_out_15), .in_2(decade1_2_out_14),
    .in_3(decade1_2_out_13), .in_4(decade1_2_out_12));
  decade1 decade1_2 (
    .in_1(and_5_out), .in_2(button_2_out), .in_3(in_3), .out_4(decade1_2_out_4), .out_5(decade1_2_out_5),
    .out_6(decade1_2_out_6), .out_7(decade1_2_out_7), .out_8(decade1_2_out_8), .out_9(decade1_2_out_9),
    .out_10(decade1_2_out_10), .out_11(decade1_2_out_11), .out_12(decade1_2_out_12),
    .out_13(decade1_2_out_13), .out_14(decade1_2_out_14), .out_15(decade1_2_out_15));
  _7_Segment_Display u_7_segment_display_14 (
    .g(comparator_1_out_26), .f(comparator_1_out_26), .a(comparator_1_out_26), .b(comparator_1_out_26),
    .e(comparator_1_out_26), .d(comparator_1_out_26), .c(comparator_1_out_26));  // open: dp
  _7_Segment_Display u_7_segment_display_15 (
    .g(n7_segemnt_13_g), .f(n7_segemnt_13_f), .a(n7_segemnt_13_a), .b(n7_segemnt_13_b), .e(n7_segemnt_13_e),
    .d(n7_segemnt_13_d), .c(n7_segemnt_13_c));  // open: dp
  _7_segemnt u_7_segemnt_13 (
    .f(n7_segemnt_13_f), .g(n7_segemnt_13_g), .e(n7_segemnt_13_e), .d(n7_segemnt_13_d), .c(n7_segemnt_13_c),
    .b(n7_segemnt_13_b), .a(n7_segemnt_13_a), .in_1(decade_5_out_11), .in_2(decade_5_out_10),
    .in_3(decade_5_out_9), .in_4(decade_5_out_8));
  _7_Segment_Display u_7_segment_display_16 (
    .g(n7_segemnt_14_g), .f(n7_segemnt_14_f), .a(n7_segemnt_14_a), .b(n7_segemnt_14_b), .e(n7_segemnt_14_e),
    .d(n7_segemnt_14_d), .c(n7_segemnt_14_c));  // open: dp
  _7_segemnt u_7_segemnt_14 (
    .f(n7_segemnt_14_f), .g(n7_segemnt_14_g), .e(n7_segemnt_14_e), .d(n7_segemnt_14_d), .c(n7_segemnt_14_c),
    .b(n7_segemnt_14_b), .a(n7_segemnt_14_a), .in_1(decade_6_out_11), .in_2(decade_6_out_10),
    .in_3(decade_6_out_9), .in_4(decade_6_out_8));
  _7_Segment_Display u_7_segment_display_17 (
    .g(n7_segemnt_15_g), .f(n7_segemnt_15_f), .a(n7_segemnt_15_a), .b(n7_segemnt_15_b), .e(n7_segemnt_15_e),
    .d(n7_segemnt_15_d), .c(n7_segemnt_15_c));  // open: dp
  _7_segemnt u_7_segemnt_15 (
    .f(n7_segemnt_15_f), .g(n7_segemnt_15_g), .e(n7_segemnt_15_e), .d(n7_segemnt_15_d), .c(n7_segemnt_15_c),
    .b(n7_segemnt_15_b), .a(n7_segemnt_15_a), .in_1(decade_7_out_11), .in_2(decade_7_out_10),
    .in_3(decade_7_out_9), .in_4(decade_7_out_8));
  _7_Segment_Display u_7_segment_display_18 (
    .g(n7_segemnt_16_g), .f(n7_segemnt_16_f), .a(n7_segemnt_16_a), .b(n7_segemnt_16_b), .e(n7_segemnt_16_e),
    .d(n7_segemnt_16_d), .c(n7_segemnt_16_c));  // open: dp
  _7_segemnt u_7_segemnt_16 (
    .f(n7_segemnt_16_f), .g(n7_segemnt_16_g), .e(n7_segemnt_16_e), .d(n7_segemnt_16_d), .c(n7_segemnt_16_c),
    .b(n7_segemnt_16_b), .a(n7_segemnt_16_a), .in_1(decade_8_out_11), .in_2(decade_8_out_10),
    .in_3(decade_8_out_9), .in_4(decade_8_out_8));
  _7_Segment_Display u_7_segment_display_19 (
    .g(n7_segemnt_17_g), .f(n7_segemnt_17_f), .a(n7_segemnt_17_a), .b(n7_segemnt_17_b), .e(n7_segemnt_17_e),
    .d(n7_segemnt_17_d), .c(n7_segemnt_17_c));  // open: dp
  _7_segemnt u_7_segemnt_17 (
    .f(n7_segemnt_17_f), .g(n7_segemnt_17_g), .e(n7_segemnt_17_e), .d(n7_segemnt_17_d), .c(n7_segemnt_17_c),
    .b(n7_segemnt_17_b), .a(n7_segemnt_17_a), .in_1(decade1_2_out_11), .in_2(decade1_2_out_10),
    .in_3(decade1_2_out_9), .in_4(decade1_2_out_8));
  _7_Segment_Display u_7_segment_display_20 (
    .g(n7_segemnt_18_g), .f(n7_segemnt_18_f), .a(n7_segemnt_18_a), .b(n7_segemnt_18_b), .e(n7_segemnt_18_e),
    .d(n7_segemnt_18_d), .c(n7_segemnt_18_c));  // open: dp
  _7_segemnt u_7_segemnt_18 (
    .f(n7_segemnt_18_f), .g(n7_segemnt_18_g), .e(n7_segemnt_18_e), .d(n7_segemnt_18_d), .c(n7_segemnt_18_c),
    .b(n7_segemnt_18_b), .a(n7_segemnt_18_a), .in_1(decade_5_out_7), .in_2(decade_5_out_6),
    .in_3(decade_5_out_5), .in_4(decade_5_out_4));
  _7_Segment_Display u_7_segment_display_21 (
    .g(n7_segemnt_19_g), .f(n7_segemnt_19_f), .a(n7_segemnt_19_a), .b(n7_segemnt_19_b), .e(n7_segemnt_19_e),
    .d(n7_segemnt_19_d), .c(n7_segemnt_19_c));  // open: dp
  _7_segemnt u_7_segemnt_19 (
    .f(n7_segemnt_19_f), .g(n7_segemnt_19_g), .e(n7_segemnt_19_e), .d(n7_segemnt_19_d), .c(n7_segemnt_19_c),
    .b(n7_segemnt_19_b), .a(n7_segemnt_19_a), .in_1(decade_6_out_7), .in_2(decade_6_out_6),
    .in_3(decade_6_out_5), .in_4(decade_6_out_4));
  _7_Segment_Display u_7_segment_display_22 (
    .g(n7_segemnt_20_g), .f(n7_segemnt_20_f), .a(n7_segemnt_20_a), .b(n7_segemnt_20_b), .e(n7_segemnt_20_e),
    .d(n7_segemnt_20_d), .c(n7_segemnt_20_c));  // open: dp
  _7_segemnt u_7_segemnt_20 (
    .f(n7_segemnt_20_f), .g(n7_segemnt_20_g), .e(n7_segemnt_20_e), .d(n7_segemnt_20_d), .c(n7_segemnt_20_c),
    .b(n7_segemnt_20_b), .a(n7_segemnt_20_a), .in_1(decade_7_out_7), .in_2(decade_7_out_6),
    .in_3(decade_7_out_5), .in_4(decade_7_out_4));
  _7_Segment_Display u_7_segment_display_23 (
    .g(n7_segemnt_21_g), .f(n7_segemnt_21_f), .a(n7_segemnt_21_a), .b(n7_segemnt_21_b), .e(n7_segemnt_21_e),
    .d(n7_segemnt_21_d), .c(n7_segemnt_21_c));  // open: dp
  _7_segemnt u_7_segemnt_21 (
    .f(n7_segemnt_21_f), .g(n7_segemnt_21_g), .e(n7_segemnt_21_e), .d(n7_segemnt_21_d), .c(n7_segemnt_21_c),
    .b(n7_segemnt_21_b), .a(n7_segemnt_21_a), .in_1(decade_8_out_7), .in_2(decade_8_out_6),
    .in_3(decade_8_out_5), .in_4(decade_8_out_4));
  _7_Segment_Display u_7_segment_display_24 (
    .g(n7_segemnt_22_g), .f(n7_segemnt_22_f), .a(n7_segemnt_22_a), .b(n7_segemnt_22_b), .e(n7_segemnt_22_e),
    .d(n7_segemnt_22_d), .c(n7_segemnt_22_c));  // open: dp
  _7_segemnt u_7_segemnt_22 (
    .f(n7_segemnt_22_f), .g(n7_segemnt_22_g), .e(n7_segemnt_22_e), .d(n7_segemnt_22_d), .c(n7_segemnt_22_c),
    .b(n7_segemnt_22_b), .a(n7_segemnt_22_a), .in_1(decade1_2_out_7), .in_2(decade1_2_out_6),
    .in_3(decade1_2_out_5), .in_4(decade1_2_out_4));

  // Notes on the sheet:
  //   Timer
  //   Team A
  //   Decade Counter
  //   Team A
  //   FINAL
  //   SCORE
  //   Comparator
  //   SECOND
  //   QUARTER
  //   THIRD 
  //   QUARTER
  //   FOURTH
  //   QUARTER
  //   FIRST
  //   QUARTER
  //   Team B
  //   Team B
endmodule

module _7_segemnt (
  input  in_1,
  input  in_2,
  input  in_3,
  input  in_4,
  output a,
  output f,
  output g,
  output b,
  output d,
  output e,
  output c
);

  wire and_1_out, and_2_out, and_3_out, and_4_out, and_5_out, not_1_out, not_2_out, not_3_out, not_4_out,
       not_5_out, not_6_out, not_7_out, not_8_out, not_9_out, not_10_out, not_11_out, not_12_out, not_13_out,
       not_14_out, not_15_out, not_16_out, not_17_out, not_18_out, not_19_out, or_1_out, or_2_out, or_3_out,
       or_5_out, or_6_out, or_8_out, or_10_out, or_11_out, or_13_out, or_14_out, or_16_out, or_17_out,
       or_19_out, or_20_out, or_22_out, or_23_out, or_24_out, or_25_out;

  not not_1 (not_1_out, or_1_out);
  not not_2 (not_2_out, or_2_out);
  not not_3 (not_3_out, or_5_out);
  not not_4 (not_4_out, or_8_out);
  not not_5 (not_5_out, or_10_out);
  or or_1 (or_1_out, in_1, in_2, in_3, in_4);
  not not_6 (not_6_out, or_13_out);
  not not_7 (not_7_out, or_16_out);
  not not_8 (not_8_out, or_19_out);
  not not_9 (not_9_out, or_22_out);
  not not_10 (not_10_out, or_24_out);
  or or_2 (or_2_out, or_3_out, not_11_out);
  not not_11 (not_11_out, and_1_out);
  and and_1 (and_1_out, in_1, in_4);
  or or_3 (or_3_out, in_2, in_3);
  or or_4 (f, not_7_out, not_6_out, not_5_out, not_3_out, not_2_out, not_1_out);
  or or_5 (or_5_out, or_6_out, not_12_out);
  not not_12 (not_12_out, in_1);
  or or_6 (or_6_out, in_2, in_3, in_4);
  or or_7 (g, not_9_out, not_8_out, not_7_out, not_6_out, not_5_out, not_3_out, not_2_out);
  or or_8 (or_8_out, not_13_out, in_1);
  not not_13 (not_13_out, and_2_out);
  and and_2 (and_2_out, in_2, in_3, in_4);
  or or_9 (e, not_9_out, not_5_out, not_3_out, not_1_out);
  or or_10 (or_10_out, not_14_out, or_11_out);
  not not_14 (not_14_out, and_3_out);
  or or_11 (or_11_out, in_1, in_4);
  and and_3 (and_3_out, in_2, in_3);
  _7_Segment_Display u_7_segment_display_1 (.g(g), .f(f), .a(a), .b(b), .e(e), .d(d), .c(c));  // open: dp
  or or_12 (d, not_9_out, not_8_out, not_6_out, not_5_out, not_3_out, not_2_out, not_1_out);
  or or_13 (or_13_out, not_15_out, or_14_out);
  not not_15 (not_15_out, and_4_out);
  or or_14 (or_14_out, in_1, in_3);
  and and_4 (and_4_out, in_2, in_4);
  or or_15 (c, not_10_out, not_8_out, not_7_out, not_6_out, not_5_out, not_4_out, not_3_out, not_2_out, not_1_out);
  or or_16 (or_16_out, or_17_out, not_16_out);
  not not_16 (not_16_out, in_2);
  or or_17 (or_17_out, in_1, in_3, in_4);
  or or_18 (b, not_10_out, not_9_out, not_8_out, not_7_out, not_4_out, not_3_out, not_2_out, not_1_out);
  or or_19 (or_19_out, or_20_out, not_17_out);
  not not_17 (not_17_out, and_5_out);
  and and_5 (and_5_out, in_3, in_4);
  or or_20 (or_20_out, in_1, in_2);
  or or_21 (a, not_1_out, not_2_out, not_3_out, not_4_out, not_5_out, not_6_out, not_8_out, not_9_out);
  or or_22 (or_22_out, or_23_out, not_18_out);
  not not_18 (not_18_out, in_3);
  or or_23 (or_23_out, in_1, in_2, in_4);
  or or_24 (or_24_out, or_25_out, not_19_out);
  not not_19 (not_19_out, in_4);
  or or_25 (or_25_out, in_1, in_2, in_3);
endmodule

module decade (
  input  in_1,
  input  in_2,
  input  in_3,
  output out_4,
  output out_5,
  output out_6,
  output out_7,
  output out_8,
  output out_9,
  output out_10,
  output out_11
);

  wire and_1_out, and_2_out, and_3_out, and_4_out, and_5_out, and_6_out, and_7_out, and_8_out, and_9_out,
       or_1_out, or_2_out, t_ff_1_qn, t_ff_2_qn, t_ff_3_qn, t_ff_4_qn, t_ff_8_qn;

  and and_1 (and_1_out, out_4, t_ff_4_qn);
  and and_2 (and_2_out, out_4, out_5);
  and and_3 (and_3_out, out_4, out_7);
  and and_4 (and_4_out, and_2_out, out_6);
  or or_1 (or_1_out, and_3_out, and_4_out);
  T_Flip_Flop t_ff_1 (.clk(in_2), .T(in_1), .Q(out_4), .Qn(t_ff_1_qn), .reset(in_3));  // open: preset, en
  T_Flip_Flop t_ff_2 (.clk(in_2), .T(and_1_out), .Q(out_5), .Qn(t_ff_2_qn), .reset(in_3));  // open: preset, en
  T_Flip_Flop t_ff_3 (.clk(in_2), .T(and_2_out), .Q(out_6), .Qn(t_ff_3_qn), .reset(in_3));  // open: preset, en
  T_Flip_Flop t_ff_4 (.clk(in_2), .T(or_1_out), .Q(out_7), .Qn(t_ff_4_qn), .reset(in_3));  // open: preset, en
  and and_5 (and_5_out, t_ff_4_qn, t_ff_3_qn, t_ff_2_qn, t_ff_1_qn);
  and and_6 (and_6_out, out_8, t_ff_8_qn);
  and and_7 (and_7_out, out_8, out_9);
  and and_8 (and_8_out, out_8, out_11);
  or or_2 (or_2_out, and_8_out, and_9_out);
  and and_9 (and_9_out, and_7_out, out_10);
  T_Flip_Flop t_ff_5 (.clk(and_5_out), .T(in_1), .Q(out_8), .reset(in_3));  // open: Qn, preset, en
  T_Flip_Flop t_ff_6 (.clk(and_5_out), .T(and_6_out), .Q(out_9), .reset(in_3));  // open: Qn, preset, en
  T_Flip_Flop t_ff_7 (.clk(and_5_out), .T(and_7_out), .Q(out_10), .reset(in_3));  // open: Qn, preset, en
  T_Flip_Flop t_ff_8 (.clk(and_5_out), .T(or_2_out), .Q(out_11), .Qn(t_ff_8_qn), .reset(in_3));  // open: preset, en
endmodule

module temp (
  input  in_1,
  input  in_2
);

  wire button_1_out, decade_1_out_4, decade_1_out_5, decade_1_out_6, decade_1_out_7, decade_1_out_8,
       decade_1_out_9, decade_1_out_10, decade_1_out_11, n7_segemnt_1_a, n7_segemnt_1_b, n7_segemnt_1_c,
       n7_segemnt_1_d, n7_segemnt_1_e, n7_segemnt_1_f, n7_segemnt_1_g, n7_segemnt_2_a, n7_segemnt_2_b,
       n7_segemnt_2_c, n7_segemnt_2_d, n7_segemnt_2_e, n7_segemnt_2_f, n7_segemnt_2_g;

  Button button_1 (.out(button_1_out));
  decade decade_1 (
    .in_1(in_1), .in_2(button_1_out), .in_3(in_2), .out_4(decade_1_out_4), .out_5(decade_1_out_5),
    .out_6(decade_1_out_6), .out_7(decade_1_out_7), .out_8(decade_1_out_8), .out_9(decade_1_out_9),
    .out_10(decade_1_out_10), .out_11(decade_1_out_11));
  _7_Segment_Display u_7_segment_display_1 (
    .g(n7_segemnt_1_g), .f(n7_segemnt_1_f), .a(n7_segemnt_1_a), .b(n7_segemnt_1_b), .e(n7_segemnt_1_e),
    .d(n7_segemnt_1_d), .c(n7_segemnt_1_c));  // open: dp
  _7_segemnt u_7_segemnt_1 (
    .f(n7_segemnt_1_f), .g(n7_segemnt_1_g), .e(n7_segemnt_1_e), .d(n7_segemnt_1_d), .c(n7_segemnt_1_c),
    .b(n7_segemnt_1_b), .a(n7_segemnt_1_a), .in_1(decade_1_out_11), .in_2(decade_1_out_10),
    .in_3(decade_1_out_9), .in_4(decade_1_out_8));
  _7_segemnt u_7_segemnt_2 (
    .f(n7_segemnt_2_f), .g(n7_segemnt_2_g), .e(n7_segemnt_2_e), .d(n7_segemnt_2_d), .c(n7_segemnt_2_c),
    .b(n7_segemnt_2_b), .a(n7_segemnt_2_a), .in_1(decade_1_out_7), .in_2(decade_1_out_6),
    .in_3(decade_1_out_5), .in_4(decade_1_out_4));
  _7_Segment_Display u_7_segment_display_2 (
    .g(n7_segemnt_2_g), .f(n7_segemnt_2_f), .a(n7_segemnt_2_a), .b(n7_segemnt_2_b), .e(n7_segemnt_2_e),
    .d(n7_segemnt_2_d), .c(n7_segemnt_2_c));  // open: dp
endmodule

module counter (
  input  in_1,
  input  in_2,
  output out_3,
  output out_4,
  output out_5,
  output out_6,
  output out_7
);

  wire and_1_out, and_2_out, and_3_out, and_4_out, decoder_1_out0, decoder_1_out1, decoder_1_out2,
       decoder_1_out3, decoder_1_out4, decoder_1_out5, decoder_1_out6, decoder_1_out7, decoder_1_out8,
       decoder_1_out9, decoder_1_out10, decoder_1_out11, decoder_1_out12, decoder_1_out13, decoder_1_out14,
       decoder_1_out15, decoder_1_out16, decoder_1_out17, decoder_1_out18, decoder_1_out19, decoder_1_out20,
       decoder_1_out21, decoder_1_out22, decoder_1_out23, decoder_1_out24, decoder_1_out25, decoder_1_out26,
       decoder_1_out27, decoder_1_out28, decoder_1_out29, decoder_1_out30, decoder_1_out31;
  wire [4:0] t_ff_1_q;

  nand nand_1 (in_1, t_ff_1_q[4], t_ff_1_q[3], t_ff_1_q[2], t_ff_1_q[1], t_ff_1_q[0]);
  and and_1 (and_1_out, in_1, t_ff_1_q[0]);
  and and_2 (and_2_out, t_ff_1_q[1], and_1_out);
  and and_3 (and_3_out, t_ff_1_q[2], and_2_out);
  and and_4 (and_4_out, t_ff_1_q[3], and_3_out);
  T_Flip_Flop t_ff_1 (.clk(in_2), .T(in_1), .Q(t_ff_1_q[0]));  // open: Qn, preset, reset, en
  T_Flip_Flop t_ff_2 (.clk(in_2), .T(and_1_out), .Q(t_ff_1_q[1]));  // open: Qn, preset, reset, en
  T_Flip_Flop t_ff_3 (.clk(in_2), .T(and_2_out), .Q(t_ff_1_q[2]));  // open: Qn, preset, reset, en
  T_Flip_Flop t_ff_4 (.clk(in_2), .T(and_3_out), .Q(t_ff_1_q[3]));  // open: Qn, preset, reset, en
  T_Flip_Flop t_ff_5 (.clk(in_2), .T(and_4_out), .Q(t_ff_1_q[4]));  // open: Qn, preset, reset, en
  Decoder #(.select(5)) decoder_1 (
    .out0(decoder_1_out0), .out1(decoder_1_out1), .out2(decoder_1_out2), .out3(decoder_1_out3),
    .out4(decoder_1_out4), .out5(decoder_1_out5), .out6(decoder_1_out6), .out7(decoder_1_out7),
    .out8(decoder_1_out8), .out9(decoder_1_out9), .out10(decoder_1_out10), .out11(decoder_1_out11),
    .out12(decoder_1_out12), .out13(decoder_1_out13), .out14(decoder_1_out14), .out15(decoder_1_out15),
    .out16(decoder_1_out16), .out17(decoder_1_out17), .out18(decoder_1_out18), .out19(decoder_1_out19),
    .out20(decoder_1_out20), .out21(decoder_1_out21), .out22(decoder_1_out22), .out23(decoder_1_out23),
    .out24(decoder_1_out24), .out25(decoder_1_out25), .out26(decoder_1_out26), .out27(decoder_1_out27),
    .out28(decoder_1_out28), .out29(decoder_1_out29), .out30(decoder_1_out30), .out31(decoder_1_out31),
    .sel(t_ff_1_q), .en(in_1));
  or or_1 (out_3, decoder_1_out0, decoder_1_out1, decoder_1_out2, decoder_1_out3, decoder_1_out4, decoder_1_out5, decoder_1_out6, decoder_1_out7);
  or or_2 (out_4, decoder_1_out8, decoder_1_out9, decoder_1_out10, decoder_1_out11, decoder_1_out13, decoder_1_out14, decoder_1_out15, decoder_1_out12);
  or or_3 (out_5, decoder_1_out16, decoder_1_out17, decoder_1_out18, decoder_1_out19, decoder_1_out20, decoder_1_out21, decoder_1_out22, decoder_1_out23);
  or or_4 (out_6, decoder_1_out24, decoder_1_out26, decoder_1_out27, decoder_1_out28, decoder_1_out29, decoder_1_out30, decoder_1_out31, decoder_1_out25);

  assign out_7 = in_1;

  // Notes on the sheet:
  //   5:32
endmodule

module decade1 (
  input  in_1,
  input  in_2,
  input  in_3,
  output out_4,
  output out_5,
  output out_6,
  output out_7,
  output out_8,
  output out_9,
  output out_10,
  output out_11,
  output out_12,
  output out_13,
  output out_14,
  output out_15
);

  wire and_1_out, and_2_out, and_3_out, and_4_out, and_5_out, and_6_out, and_7_out, and_8_out, and_9_out,
       and_10_out, and_11_out, and_12_out, and_13_out, and_14_out, or_1_out, or_2_out, or_3_out, t_ff_1_qn,
       t_ff_2_qn, t_ff_3_qn, t_ff_4_qn, t_ff_5_qn, t_ff_6_qn, t_ff_7_qn, t_ff_8_qn, t_ff_12_qn;

  and and_1 (and_1_out, out_4, t_ff_4_qn);
  and and_2 (and_2_out, out_4, out_5);
  and and_3 (and_3_out, out_4, out_7);
  and and_4 (and_4_out, and_2_out, out_6);
  or or_1 (or_1_out, and_3_out, and_4_out);
  T_Flip_Flop t_ff_1 (.clk(in_2), .T(in_1), .Q(out_4), .Qn(t_ff_1_qn), .reset(in_3));  // open: preset, en
  T_Flip_Flop t_ff_2 (.clk(in_2), .T(and_1_out), .Q(out_5), .Qn(t_ff_2_qn), .reset(in_3));  // open: preset, en
  T_Flip_Flop t_ff_3 (.clk(in_2), .T(and_2_out), .Q(out_6), .Qn(t_ff_3_qn), .reset(in_3));  // open: preset, en
  T_Flip_Flop t_ff_4 (.clk(in_2), .T(or_1_out), .Q(out_7), .Qn(t_ff_4_qn), .reset(in_3));  // open: preset, en
  and and_5 (and_5_out, t_ff_4_qn, t_ff_3_qn, t_ff_2_qn, t_ff_1_qn);
  and and_6 (and_6_out, out_8, t_ff_8_qn);
  and and_7 (and_7_out, out_8, out_9);
  and and_8 (and_8_out, out_8, out_11);
  or or_2 (or_2_out, and_8_out, and_9_out);
  and and_9 (and_9_out, and_7_out, out_10);
  T_Flip_Flop t_ff_5 (.clk(and_5_out), .T(in_1), .Q(out_8), .Qn(t_ff_5_qn), .reset(in_3));  // open: preset, en
  T_Flip_Flop t_ff_6 (.clk(and_5_out), .T(and_6_out), .Q(out_9), .Qn(t_ff_6_qn), .reset(in_3));  // open: preset, en
  T_Flip_Flop t_ff_7 (.clk(and_5_out), .T(and_7_out), .Q(out_10), .Qn(t_ff_7_qn), .reset(in_3));  // open: preset, en
  T_Flip_Flop t_ff_8 (.clk(and_5_out), .T(or_2_out), .Q(out_11), .Qn(t_ff_8_qn), .reset(in_3));  // open: preset, en
  and and_10 (and_10_out, t_ff_5_qn, t_ff_6_qn, t_ff_7_qn, t_ff_8_qn);
  and and_11 (and_11_out, out_12, t_ff_12_qn);
  and and_12 (and_12_out, out_12, out_13);
  and and_13 (and_13_out, out_12, out_15);
  and and_14 (and_14_out, and_12_out, out_14);
  or or_3 (or_3_out, and_13_out, and_14_out);
  T_Flip_Flop t_ff_9 (.clk(and_10_out), .T(in_1), .Q(out_12), .reset(in_3));  // open: Qn, preset, en
  T_Flip_Flop t_ff_10 (.clk(and_10_out), .T(and_11_out), .Q(out_13), .reset(in_3));  // open: Qn, preset, en
  T_Flip_Flop t_ff_11 (.clk(and_10_out), .T(and_12_out), .Q(out_14), .reset(in_3));  // open: Qn, preset, en
  T_Flip_Flop t_ff_12 (.clk(and_10_out), .T(or_3_out), .Q(out_15), .Qn(t_ff_12_qn), .reset(in_3));  // open: preset, en
endmodule

module display (
  input  in_1
);

  wire undriven, undriven_2;
  wire [3:0] undriven_3;

  _7_Segment_Display u_7_segment_display_1 (
    .g(in_1), .f(in_1), .a(in_1), .b(in_1), .e(in_1), .d(undriven), .c(in_1));  // open: dp
  Hex_Digit_Display hex_digit_display_1 (.value(undriven_3), .dp(undriven_2));
endmodule

module comparator (
  input  in_1,
  input  in_2,
  input  in_3,
  input  in_4,
  input  in_5,
  input  in_6,
  input  in_7,
  input  in_8,
  input  in_9,
  input  in_10,
  input  in_11,
  input  in_12,
  input  in_13,
  input  in_14,
  input  in_15,
  input  in_16,
  input  in_17,
  input  in_18,
  input  in_19,
  input  in_20,
  input  in_21,
  input  in_22,
  input  in_23,
  input  in_24,
  output out_25,
  output out_26,
  output out_27
);

  wire and_1_out, and_2_out, and_3_out, and_4_out, comparator_1_eq, comparator_1_gt, comparator_1_lt,
       comparator_2_eq, comparator_2_gt, comparator_2_lt, comparator_3_eq, comparator_3_gt, comparator_3_lt;

  Comparator #(.width(4), .mode("unsigned")) comparator_1 (
    .a({in_5, in_3, in_2, in_1}), .b({in_8, in_7, in_6, in_4}), .gt(comparator_1_gt), .eq(comparator_1_eq),
    .lt(comparator_1_lt));
  Comparator #(.width(4), .mode("unsigned")) comparator_2 (
    .a({in_16, in_14, in_12, in_10}), .b({in_15, in_13, in_11, in_9}), .gt(comparator_2_gt),
    .eq(comparator_2_eq), .lt(comparator_2_lt));
  Comparator #(.width(4), .mode("unsigned")) comparator_3 (
    .a({in_24, in_23, in_21, in_19}), .b({in_22, in_20, in_18, in_17}), .gt(comparator_3_gt),
    .eq(comparator_3_eq), .lt(comparator_3_lt));
  and and_1 (and_1_out, comparator_2_eq, comparator_1_eq, comparator_3_lt);
  and and_2 (and_2_out, comparator_2_lt, comparator_1_eq);
  or or_1 (out_26, and_1_out, and_2_out, comparator_1_lt);
  and and_3 (and_3_out, comparator_2_gt, comparator_1_eq);
  and and_4 (and_4_out, comparator_3_gt, comparator_1_eq, comparator_2_eq);
  and and_5 (out_25, comparator_1_eq, comparator_2_eq, comparator_3_eq);
  or or_2 (out_27, and_4_out, and_3_out, comparator_1_gt);
endmodule

module random (
  input  in_1,
  output [7:0] out_2,
  output [7:0] out_3,
  output [7:0] out_4,
  output [7:0] out_5,
  output [7:0] out_6,
  output [7:0] out_7,
  output [7:0] out_8,
  output [7:0] out_9,
  output [7:0] out_10,
  output [7:0] out_11,
  output [7:0] out_12,
  output [7:0] out_13
);

  wire button_1_out, button_2_out, button_3_out, button_4_out, button_5_out, button_6_out, button_7_out,
       button_8_out, button_9_out, undriven, undriven_2, undriven_3;

  Counter counter_1 (.load(1'b1), .count(in_1), .Q(out_5), .clk(button_1_out));  // open: D, carry, clr
  Button button_1 (.out(button_1_out));
  Counter counter_2 (.load(1'b1), .count(in_1), .Q(out_8), .clk(button_3_out));  // open: D, carry, clr
  Button button_2 (.out(button_2_out));
  Button button_3 (.out(button_3_out));
  Counter counter_3 (.load(1'b1), .count(in_1), .Q(out_6), .clk(button_2_out));  // open: D, carry, clr
  Counter counter_4 (.load(1'b1), .count(in_1), .Q(out_9), .clk(button_4_out));  // open: D, carry, clr
  Button button_4 (.out(button_4_out));
  Counter counter_5 (.load(1'b1), .count(in_1), .Q(out_7), .clk(button_5_out));  // open: D, carry, clr
  Button button_5 (.out(button_5_out));
  Counter counter_6 (.load(1'b1), .count(in_1), .Q(out_10), .clk(button_7_out));  // open: D, carry, clr
  Button button_6 (.out(button_6_out));
  Button button_7 (.out(button_7_out));
  Counter counter_7 (.load(1'b1), .count(in_1), .Q(out_11), .clk(button_8_out));  // open: D, carry, clr
  Counter counter_8 (.load(1'b1), .count(in_1), .Q(out_2), .clk(button_6_out));  // open: D, carry, clr
  Button button_8 (.out(button_8_out));
  Counter counter_9 (.load(1'b1), .count(in_1), .Q(out_3), .clk(button_9_out));  // open: D, carry, clr
  Button button_9 (.out(button_9_out));
  Counter counter_10 (.load(1'b1), .count(in_1), .Q(out_12), .clk(undriven));  // open: D, carry, clr
  Counter counter_11 (.load(1'b1), .count(in_1), .Q(out_13), .clk(undriven_3));  // open: D, carry, clr
  Counter counter_12 (.load(1'b1), .count(in_1), .Q(out_4), .clk(undriven_2));  // open: D, carry, clr
endmodule
